# Fritzing sketch circuit (saved by Fritzing 0.9.3b)
breadboards: 2

parts:
  Part1 = Arduino Uno (Rev3)
  Driver1 = 28BYJ-48 Driver Module [part_number=ULN2003 package=THT]
  SM1 = 28BYJ-48 Stepper Motor [part_number=28BYJ-48]
  Driver2 = 28BYJ-48 Driver Module [part_number=ULN2003 package=THT]
  SM2 = 28BYJ-48 Stepper Motor [part_number=28BYJ-48]  # not connected
  Driver3 = 28BYJ-48 Driver Module [part_number=ULN2003 package=THT]
  SM3 = 28BYJ-48 Stepper Motor [part_number=28BYJ-48]
  U1 = SWITCH_SPDT [package=kps-1290]
  C1 = Capacitor [package=cap-pth-small2]
  R1 = Resistor [tolerance=±5% resistance=4.7k package="2512 [SMD]"]
  U2 = SWITCH_SPDT [package=kps-1290]
  U3 = SWITCH_SPDT [package=kps-1290]
  Power_plug1 = Power plug
  C3 = Capacitor [package=cap-pth-small2]
  R3 = Resistor [tolerance=±5% resistance=4.7k package="2512 [SMD]"]
  J1 = Basic Servo

nets:
  N1: Part1.A0, Driver2.IN1, Driver3.IN4
  N2: Part1.A1, Driver2.IN2, Driver3.IN3
  N3: Part1.A2, Driver2.IN3, Driver3.IN2
  N4: Part1.A3, Driver2.IN4, Driver3.IN1
  N5: Part1.D9_PWM, U2.P, C3.2, R3.Pin_0
  N6: Part1.D10_PWM/SS, U1.P, C1.2, R1.Pin_0, U3.P
  N7: Part1.D11_PWM/MOSI, J1.pulse
  N8: Part1.D2, Driver1.IN4
  N9: Part1.D3_PWM, Driver1.IN3
  N10: Part1.D4, Driver1.IN2
  N11: Part1.D5_PWM, Driver1.IN1
  GND: Part1.GND, Driver2.GND, Driver3.GND, U2.O, Power_plug1.GND, C3.1, J1.gnd
  N12: Driver1.blue-pin, SM1.blue-pin
  N13: Driver1.pink-pin, SM1.pink-pin
  N14: Driver1.yellow-pin, SM1.yellow-pin
  N15: Driver1.orange-pin, SM1.orange-pin
  N16: Driver1.red-pin, SM1.red-pin
  VCC: Driver2.Vmotor, Driver3.Vmotor, R1.Pin_1, Power_plug1.VCC, R3.Pin_1, J1.vcc
  N17: Driver3.blue-pin, SM3.blue-pin
  N18: Driver3.pink-pin, SM3.pink-pin
  N19: Driver3.yellow-pin, SM3.yellow-pin
  N20: Driver3.orange-pin, SM3.orange-pin
  N21: Driver3.red-pin, SM3.red-pin
  N22: U1.O, C1.1, U3.O

notes:
  C NO NC
  Limit X
  Limit Y1,Y2
  Steppers Y1,Y2
  Stepper X
  Sg90 Servo(pen)
  USB Power Supply (5V, ~1A)

custom parts:
  28BYJ-48 Driver Module: ULN2003 Driver Module for the 28BYJ-48 Unipolar Stepper Motor LED A - Blue wire - Bottom coil left LED B - Pink wire - Top coil left LED C - Yellow wire - Bottom coil right LED D - Orange wire - Top coil right Common rail - red Connector pins: blue - pink - yellow - orange - red Control pins - IN1 to IN4 Power pins - GND & Vmotor (5-12V) On/Off jumper (if removed, power to motor is cut).
  28BYJ-48 Stepper Motor: Unipolar Stepper Motor 28BYJ-48 Top coil - pink & orange Bottom coil - blue & yellow Common rail - red Connector pins: blue - pink - yellow - orange - red
